// Logisim project GuessTheNumberXTREME.circ as structural Verilog: 20 circuits, main circuit main
module cronometro0a9 (
  input  Mode,
  input  CLK,
  input  Enable,
  input  Clear,
  output [3:0] Saida_Display,
  output Saida_C
);

  wire somador0a9_1_s0, somador0a9_1_s1, somador0a9_1_s2, somador0a9_1_s3;

  D_Flip_Flop #(.enable("true")) d_ff_1 (
    .clk(CLK), .D(somador0a9_1_s3), .Q(Saida_Display[3]), .en(Enable), .reset(Clear));  // open: Qn, preset
  D_Flip_Flop #(.enable("true")) d_ff_2 (
    .clk(CLK), .D(somador0a9_1_s2), .Q(Saida_Display[2]), .en(Enable), .reset(Clear));  // open: Qn, preset
  D_Flip_Flop #(.enable("true")) d_ff_3 (
    .clk(CLK), .D(somador0a9_1_s1), .Q(Saida_Display[1]), .en(Enable), .reset(Clear));  // open: Qn, preset
  D_Flip_Flop #(.enable("true")) d_ff_4 (
    .clk(CLK), .D(somador0a9_1_s0), .Q(Saida_Display[0]), .en(Enable), .reset(Clear));  // open: Qn, preset
  Somador0a9 somador0a9_1 (
    .mode(Mode), .a3(Saida_Display[3]), .a2(Saida_Display[2]), .a1(Saida_Display[1]), .a0(Saida_Display[0]),
    .s3(somador0a9_1_s3), .s2(somador0a9_1_s2), .s1(somador0a9_1_s1), .s0(somador0a9_1_s0), .c(Saida_C));
endmodule

module main (
);

  wire A0, A1, A2, A3, A___JOGANDO, A_VENCEU, ACERTOU, B0, B1, B2, B3, B___JOGANDO, B_VENCEU, CHUTANDO_X,
       CHUTANDO_Y, CHUTAR, CLK, CONFIGURAR, DESLIGADO, DM, DMA, DMB, DS, DSA, DSB, EM_JOGO, EMPATE, ENDA,
       ENDB, FIM_DE_JOGO, IGUAL, MAIOR, MENOR, NA, NB, NX, NY, or_1_out, or_2_out, PROXIMO, RESET, START,
       tunnel, UM, UMA, UMB, US, USA, USB;
  wire [3:0] dma_t, dmb_t, dsa_t, dsb_t, JA, JB, PA, PB, uma_t, umb_t, usa_t, usb_t, X, Y;

  Clock clock_1 (.out(CLK));
  or or_1 (or_1_out, START, RESET);
  timer timer_1 (
    .Enable(B___JOGANDO), .Clear(RESET), .DM(DM), .UM(UM), .DS(DS), .US(US), .Mode(tunnel), .UMX(uma_t),
    .DSX(dsa_t), .USX(usa_t), .CLK(CLK), .DMX(dma_t), .End(ENDA));
  Conversor_Negativo conversor_negativo_1 (
    .neg(NA), .s3(JA[3]), .s2(JA[2]), .s1(JA[1]), .s0(JA[0]), .in_1({A3, A2, A1, A0}));
  or or_2 (or_2_out, CONFIGURAR, START);
  S_R_Flip_Flop #(.Pre_Clr_Positions("LEGACY"), .NewFFLayout("false")) s_r_ff_1 (
    .S(START), .clk(or_1_out), .R(RESET), .Q(EM_JOGO), .Qn(DESLIGADO), .reset(FIM_DE_JOGO));  // open: preset
  Button button_1 (.out(DMA));
  Hex_Digit_Display hex_digit_display_1 (.value(dma_t));  // open: dp
  S_R_Flip_Flop #(.Pre_Clr_Positions("LEGACY"), .NewFFLayout("false")) s_r_ff_2 (
    .S(CONFIGURAR), .clk(or_2_out), .R(START), .Q(tunnel), .reset(RESET));  // open: Qn, preset
  Hex_Digit_Display hex_digit_display_2 (.value(PA));  // open: dp
  Button button_2 (.out(UMA));
  LED led_1 (.in(1'b1));
  LED led_2 (.in(1'b1));
  Hex_Digit_Display hex_digit_display_3 (.value(uma_t));  // open: dp
  _7_Segment_Display u_7_segment_display_1 (.g(NA));  // open: f, a, b, e, d, c, dp
  Hex_Digit_Display hex_digit_display_4 (.value(JA));  // open: dp
  // DipSwitch dipswitch_1: pin names not known; wires that end beside it: A3, A2, A1, A0
  LED led_3 (.in(A___JOGANDO));
  Button button_3 (.out(DSA));
  Button button_4 (.out(USA));
  Hex_Digit_Display hex_digit_display_5 (.value(dsa_t));  // open: dp
  Hex_Digit_Display hex_digit_display_6 (.value(usa_t));  // open: dp
  Placar placar_1 (
    .ACERTOU(ACERTOU), .A___JOGANDO(A___JOGANDO), .B___JOGANDO(B___JOGANDO), .RESET(RESET), .END_A(ENDA),
    .END_B(ENDB), .FIM_DE_JOGO(FIM_DE_JOGO), .A_Ganhou(A_VENCEU), .EMPATE(EMPATE), .B_Ganhou(B_VENCEU),
    .Placar_A(PA), .Placar_B(PB));
  LED led_4 (.in(A_VENCEU));
  Button button_5 (.out(START));
  LED led_5 (.in(MAIOR));
  _7_Segment_Display u_7_segment_display_2 (.g(NX));  // open: f, a, b, e, d, c, dp
  Hex_Digit_Display hex_digit_display_7 (.value(X));  // open: dp
  LED led_6 (.in(CHUTANDO_X));
  LED led_7 (.in(FIM_DE_JOGO));
  LED led_8 (.in(EMPATE));
  LED led_9 (.in(tunnel));
  Button button_6 (.out(CONFIGURAR));
  LED led_10 (.in(ACERTOU));
  LED led_11 (.in(IGUAL));
  Button button_7 (.out(CHUTAR));
  Button button_8 (.out(PROXIMO));
  _7_Segment_Display u_7_segment_display_3 (.g(NY));  // open: f, a, b, e, d, c, dp
  LED led_12 (.in(B_VENCEU));
  Button button_9 (.out(RESET));
  LED led_13 (.in(MENOR));
  Hex_Digit_Display hex_digit_display_8 (.value(Y));  // open: dp
  LED led_14 (.in(CHUTANDO_Y));
  timer timer_2 (
    .Enable(A___JOGANDO), .Clear(RESET), .DM(DM), .UM(UM), .DS(DS), .US(US), .Mode(tunnel), .UMX(umb_t),
    .DSX(dsb_t), .USX(usb_t), .CLK(CLK), .DMX(dmb_t), .End(ENDB));
  Button button_10 (.out(DMB));
  Hex_Digit_Display hex_digit_display_9 (.value(dmb_t));  // open: dp
  Conversor_Negativo conversor_negativo_2 (
    .neg(NB), .s3(JB[3]), .s2(JB[2]), .s1(JB[1]), .s0(JB[0]), .in_1({B3, B2, B1, B0}));
  Button button_11 (.out(UMB));
  Hex_Digit_Display hex_digit_display_10 (.value(umb_t));  // open: dp
  _7_Segment_Display u_7_segment_display_4 (.g(NB));  // open: f, a, b, e, d, c, dp
  // DipSwitch dipswitch_2: pin names not known; wires that end beside it: B3, B2, B1, B0
  or or_3 (DM, DMA, DMB);
  Hex_Digit_Display hex_digit_display_11 (.value(PB));  // open: dp
  Button button_12 (.out(DSB));
  LED led_15 (.in(1'b1));
  LED led_16 (.in(1'b1));
  Hex_Digit_Display hex_digit_display_12 (.value(dsb_t));  // open: dp
  Hex_Digit_Display hex_digit_display_13 (.value(JB));  // open: dp
  LED led_17 (.in(B___JOGANDO));
  or or_4 (DS, DSA, DSB);
  Circuito_Core circuito_core_1 (
    .PROXIMO(PROXIMO), .X(CHUTANDO_X), .Y(CHUTANDO_Y), .B(B___JOGANDO), .START(EM_JOGO),
    .JA({A3, A2, A1, A0}), .JB({B3, B2, B1, B0}), .END_A(ENDA), .RESET(RESET), .A(A___JOGANDO), .NX(NX),
    .NY(NY), .Y_2(Y), .X_2(X), .MAIOR(MAIOR), .IGUAL(IGUAL), .MENOR(MENOR), .END_B(ENDB), .CHUTAR(CHUTAR),
    .ACERTOU(ACERTOU));  // open: COMP
  Button button_13 (.out(USB));
  Hex_Digit_Display hex_digit_display_14 (.value(usb_t));  // open: dp
  or or_5 (UM, UMA, UMB);
  or or_6 (US, USA, USB);

  // Other names for the same wires on the sheet: NUMA[3:0] = {A3, A2, A1, A0}; NUMB[3:0] = {B3, B2, B1, B0}

  // Notes on the sheet:
  //   CRONÔMETRO A
  //   JOGADOR - A
  //   PLACAR - A
  //   CRONÔMETRO A
  //   JOGADA
  //   NUMEROS DA JOGADA
  //   CRONÔMETRO B
  //   JOGADOR - B
  //   PLACAR - B
  //   CRONÔMETRO B
  //   JOGADA
endmodule

module timer (
  input  Mode,
  input  Enable,
  input  Clear,
  input  CLK,
  input  DM,
  input  UM,
  input  DS,
  input  US,
  output [3:0] DMX,
  output [3:0] UMX,
  output [3:0] DSX,
  output [3:0] USX,
  output End
);

  wire and_1_out, and_2_out, and_3_out, and_4_out, and_5_out, and_6_out, and_7_out, and_8_out, and_9_out,
       and_10_out, and_11_out, cronometro0a5_1_saida_c, cronometro0a5_2_saida_c, cronometro0a9_1_saida_c,
       cronometro0a9_2_saida_c, n4to1bit_1_out_2, n4to1bit_2_out_2, n4to1bit_3_out_2, n4to1bit_4_out_2,
       not_1_out, not_2_out, not_3_out, not_4_out, or_1_out, or_2_out, or_3_out, or_4_out, or_5_out,
       validador_cronometro_1_dm_2, validador_cronometro_1_ds_2, validador_cronometro_1_um_2,
       validador_cronometro_1_us_2;

  or or_1 (or_1_out, Mode, not_1_out);
  validador_cronometro validador_cronometro_1 (
    .DM(cronometro0a5_1_saida_c), .UM(cronometro0a9_1_saida_c), .DS(cronometro0a5_2_saida_c),
    .US(cronometro0a9_2_saida_c), .DM_2(validador_cronometro_1_dm_2), .UM_2(validador_cronometro_1_um_2),
    .DS_2(validador_cronometro_1_ds_2), .US_2(validador_cronometro_1_us_2));
  not not_1 (not_1_out, Enable);
  or or_2 (or_2_out, and_1_out, and_2_out);
  and and_1 (and_1_out, DM, Mode);
  cronometro0a5 cronometro0a5_1 (
    .CLK(or_2_out), .Enable(or_1_out), .Clear(Clear), .Mode(Mode), .Saida_Display(DMX),
    .Saida_C(cronometro0a5_1_saida_c));
  or or_3 (or_3_out, and_3_out, and_4_out);
  and and_2 (and_2_out, validador_cronometro_1_dm_2, cronometro0a9_1_saida_c);
  and and_3 (and_3_out, UM, Mode);
  cronometro0a9 cronometro0a9_1 (
    .CLK(or_3_out), .Enable(or_1_out), .Clear(Clear), .Mode(Mode), .Saida_Display(UMX),
    .Saida_C(cronometro0a9_1_saida_c));
  and and_4 (and_4_out, validador_cronometro_1_um_2, cronometro0a5_2_saida_c);
  and and_5 (and_5_out, DS, Mode);
  cronometro0a5 cronometro0a5_2 (
    .CLK(or_4_out), .Enable(or_1_out), .Clear(Clear), .Mode(Mode), .Saida_Display(DSX),
    .Saida_C(cronometro0a5_2_saida_c));
  or or_4 (or_4_out, and_5_out, and_6_out);
  and and_6 (and_6_out, validador_cronometro_1_ds_2, cronometro0a9_2_saida_c);
  and and_7 (and_7_out, US, Mode);
  cronometro0a9 cronometro0a9_2 (
    .CLK(or_5_out), .Enable(or_1_out), .Clear(Clear), .Mode(Mode), .Saida_Display(USX),
    .Saida_C(cronometro0a9_2_saida_c));
  or or_5 (or_5_out, and_7_out, and_8_out);
  and and_8 (and_8_out, validador_cronometro_1_us_2, and_9_out);
  and and_9 (and_9_out, ~Mode, ~and_10_out, and_11_out);  // AND_Gate
  and and_10 (and_10_out, n4to1bit_3_out_2, n4to1bit_1_out_2, ~Mode, n4to1bit_2_out_2, n4to1bit_4_out_2);  // AND_Gate
  and and_11 (and_11_out, not_3_out, CLK);
  _4to1bit u_4to1bit_1 (.in_1(UMX), .out_2(n4to1bit_1_out_2));
  _4to1bit u_4to1bit_2 (.in_1(DSX), .out_2(n4to1bit_2_out_2));
  _4to1bit u_4to1bit_3 (.in_1(DMX), .out_2(n4to1bit_3_out_2));
  and and_12 (End, n4to1bit_3_out_2, n4to1bit_1_out_2, n4to1bit_2_out_2, n4to1bit_4_out_2);
  not not_2 (not_2_out, not_4_out);
  not not_3 (not_3_out, not_2_out);
  not not_4 (not_4_out, CLK);
  _4to1bit u_4to1bit_4 (.in_1(USX), .out_2(n4to1bit_4_out_2));
endmodule

module Somador0a9 (
  input  mode,
  input  a3,
  input  a2,
  input  a1,
  input  a0,
  output s3,
  output s2,
  output s1,
  output s0,
  output c
);

  wire and_1_out, and_2_out, and_3_out, and_4_out, and_5_out, and_6_out, and_7_out, and_8_out, and_9_out,
       and_10_out, and_11_out, and_12_out, and_13_out, and_14_out, and_15_out, and_16_out, and_17_out,
       and_18_out, and_19_out, and_20_out, not_1_out, not_2_out, not_3_out, not_4_out, not_5_out, not_6_out,
       not_7_out, not_8_out, not_9_out, not_10_out, not_11_out, not_12_out, not_13_out, not_14_out,
       not_15_out, not_16_out, not_17_out, not_18_out, not_19_out, not_20_out, not_21_out, not_22_out,
       not_23_out, not_24_out, not_25_out, not_26_out, not_27_out, not_28_out, not_29_out, not_30_out,
       not_31_out, not_32_out, not_33_out, not_34_out, not_35_out, not_36_out, not_37_out, not_38_out,
       not_39_out, not_40_out, not_41_out, not_42_out, not_43_out, not_44_out, not_45_out;

  not not_1 (not_1_out, mode);
  not not_2 (not_2_out, a3);
  not not_3 (not_3_out, a2);
  not not_4 (not_4_out, a1);
  not not_5 (not_5_out, a0);
  not not_6 (not_6_out, mode);
  not not_7 (not_7_out, mode);
  not not_8 (not_8_out, mode);
  not not_9 (not_9_out, a3);
  not not_10 (not_10_out, a2);
  not not_11 (not_11_out, a1);
  not not_12 (not_12_out, a0);
  not not_13 (not_13_out, mode);
  not not_14 (not_14_out, mode);
  not not_15 (not_15_out, mode);
  not not_16 (not_16_out, a2);
  not not_17 (not_17_out, a1);
  not not_18 (not_18_out, a0);
  not not_19 (not_19_out, a3);
  not not_20 (not_20_out, a2);
  not not_21 (not_21_out, a3);
  not not_22 (not_22_out, a1);
  not not_23 (not_23_out, a3);
  not not_24 (not_24_out, a0);
  not not_25 (not_25_out, mode);
  not not_26 (not_26_out, mode);
  not not_27 (not_27_out, a1);
  not not_28 (not_28_out, a0);
  not not_29 (not_29_out, mode);
  not not_30 (not_30_out, a1);
  not not_31 (not_31_out, a0);
  not not_32 (not_32_out, a3);
  not not_33 (not_33_out, a1);
  not not_34 (not_34_out, a3);
  not not_35 (not_35_out, a0);
  not not_36 (not_36_out, mode);
  not not_37 (not_37_out, a0);
  not not_38 (not_38_out, a3);
  not not_39 (not_39_out, a0);
  not not_40 (not_40_out, a2);
  not not_41 (not_41_out, a1);
  not not_42 (not_42_out, a0);
  not not_43 (not_43_out, mode);
  not not_44 (not_44_out, a2);
  not not_45 (not_45_out, a1);
  and and_1 (and_1_out, not_1_out, not_2_out, not_3_out, not_4_out, not_5_out);
  and and_2 (and_2_out, not_6_out, a3, a0);
  and and_3 (and_3_out, not_7_out, a3, a1);
  and and_4 (and_4_out, not_8_out, a3, a2);
  and and_5 (and_5_out, mode, not_9_out, a2, a1, a0);
  and and_6 (and_6_out, mode, a3, not_10_out, not_11_out, not_12_out);
  and and_7 (and_7_out, not_13_out, a2, a0);
  and and_8 (and_8_out, not_14_out, a2, a1);
  and and_9 (and_9_out, not_15_out, a3, not_16_out, not_17_out, not_18_out);
  and and_10 (and_10_out, mode, not_19_out, not_20_out, a1, a0);
  and and_11 (and_11_out, mode, not_21_out, a2, not_22_out);
  and and_12 (and_12_out, mode, not_23_out, a2, not_24_out);
  and and_13 (and_13_out, not_25_out, a1, a0);
  and and_14 (and_14_out, not_26_out, a2, not_27_out, not_28_out);
  and and_15 (and_15_out, not_29_out, a3, not_30_out, not_31_out);
  and and_16 (and_16_out, mode, not_32_out, not_33_out, a0);
  and and_17 (and_17_out, mode, not_34_out, a1, not_35_out);
  and and_18 (and_18_out, not_36_out, not_37_out);
  and and_19 (and_19_out, not_38_out, not_39_out);
  and and_20 (and_20_out, not_40_out, not_41_out, not_42_out);
  and and_21 (c, not_43_out, a3, not_44_out, not_45_out, a0);
  or or_1 (s3, and_1_out, and_2_out, and_3_out, and_4_out, and_5_out, and_6_out);
  or or_2 (s2, and_7_out, and_8_out, and_9_out, and_10_out, and_11_out, and_12_out);
  or or_3 (s1, and_13_out, and_14_out, and_15_out, and_16_out, and_17_out);
  or or_4 (s0, and_18_out, and_19_out, and_20_out);
endmodule

module Somador0a5 (
  input  mode,
  input  a3,
  input  a2,
  input  a1,
  input  a0,
  output s3,
  output s2,
  output s1,
  output s0,
  output c
);

  wire and_1_out, and_2_out, and_3_out, and_4_out, and_5_out, and_6_out, and_7_out, and_8_out, and_9_out,
       and_10_out, and_11_out, and_12_out, not_1_out, not_2_out, not_3_out, not_4_out, not_5_out, not_6_out,
       not_7_out, not_8_out, not_9_out, not_10_out, not_11_out, not_12_out, not_13_out, not_14_out,
       not_15_out, not_16_out, not_17_out, not_18_out, not_19_out, not_20_out, not_21_out, not_22_out,
       not_23_out, not_24_out, not_25_out, not_26_out, not_27_out, not_28_out, not_29_out, not_30_out,
       not_31_out, not_32_out, not_33_out, not_34_out, not_35_out, not_36_out;

  not not_1 (not_1_out, mode);
  not not_2 (not_2_out, a3);
  not not_3 (not_3_out, a2);
  not not_4 (not_4_out, a1);
  not not_5 (not_5_out, a0);
  not not_6 (not_6_out, mode);
  not not_7 (not_7_out, a3);
  not not_8 (not_8_out, a1);
  not not_9 (not_9_out, a3);
  not not_10 (not_10_out, a2);
  not not_11 (not_11_out, a3);
  not not_12 (not_12_out, a1);
  not not_13 (not_13_out, a0);
  not not_14 (not_14_out, mode);
  not not_15 (not_15_out, a3);
  not not_16 (not_16_out, a2);
  not not_17 (not_17_out, mode);
  not not_18 (not_18_out, a3);
  not not_19 (not_19_out, a1);
  not not_20 (not_20_out, a0);
  not not_21 (not_21_out, a3);
  not not_22 (not_22_out, a2);
  not not_23 (not_23_out, a1);
  not not_24 (not_24_out, a3);
  not not_25 (not_25_out, a2);
  not not_26 (not_26_out, a0);
  not not_27 (not_27_out, a3);
  not not_28 (not_28_out, a2);
  not not_29 (not_29_out, a0);
  not not_30 (not_30_out, a3);
  not not_31 (not_31_out, a1);
  not not_32 (not_32_out, a0);
  not not_33 (not_33_out, mode);
  not not_34 (not_34_out, a3);
  not not_35 (not_35_out, a1);
  not not_36 (not_36_out, mode);
  and and_1 (and_1_out, not_1_out, not_2_out, not_3_out, not_4_out, not_5_out);
  and and_2 (and_2_out, not_6_out, not_7_out, a2, not_8_out, a0);
  and and_3 (and_3_out, mode, not_9_out, not_10_out, a1, a0);
  and and_4 (and_4_out, mode, not_11_out, a2, not_12_out, not_13_out);
  and and_5 (and_5_out, not_14_out, not_15_out, not_16_out, a1, a0);
  and and_6 (and_6_out, not_17_out, not_18_out, a2, not_19_out, not_20_out);
  and and_7 (and_7_out, mode, not_21_out, not_22_out, not_23_out, a0);
  and and_8 (and_8_out, mode, not_24_out, not_25_out, a1, not_26_out);
  and and_9 (and_9_out, not_27_out, not_28_out, not_29_out);
  and and_10 (and_10_out, not_30_out, not_31_out, not_32_out);
  and and_11 (and_11_out, not_33_out, not_34_out, a2, not_35_out, a0);
  and and_12 (and_12_out, not_36_out, a3, a2, a1, a0);
  or or_1 (s2, and_1_out, and_2_out, and_3_out, and_4_out);
  or or_2 (s1, and_5_out, and_6_out, and_7_out, and_8_out);
  or or_3 (s0, and_9_out, and_10_out);
  or or_4 (c, and_11_out, and_12_out);

  assign s3 = 1'b0;
endmodule

module cronometro0a5 (
  input  Mode,
  input  CLK,
  input  Enable,
  input  Clear,
  output [3:0] Saida_Display,
  output Saida_C
);

  wire somador0a5_1_s0, somador0a5_1_s1, somador0a5_1_s2, somador0a5_1_s3;

  D_Flip_Flop #(.enable("true")) d_ff_1 (
    .clk(CLK), .D(somador0a5_1_s3), .Q(Saida_Display[3]), .en(Enable), .reset(Clear));  // open: Qn, preset
  D_Flip_Flop #(.enable("true")) d_ff_2 (
    .clk(CLK), .D(somador0a5_1_s2), .Q(Saida_Display[2]), .en(Enable), .reset(Clear));  // open: Qn, preset
  D_Flip_Flop #(.enable("true")) d_ff_3 (
    .clk(CLK), .D(somador0a5_1_s1), .Q(Saida_Display[1]), .en(Enable), .reset(Clear));  // open: Qn, preset
  D_Flip_Flop #(.enable("true")) d_ff_4 (
    .clk(CLK), .D(somador0a5_1_s0), .Q(Saida_Display[0]), .en(Enable), .reset(Clear));  // open: Qn, preset
  Somador0a5 somador0a5_1 (
    .mode(Mode), .s3(somador0a5_1_s3), .a3(Saida_Display[3]), .a2(Saida_Display[2]), .a1(Saida_Display[1]),
    .a0(Saida_Display[0]), .s2(somador0a5_1_s2), .s1(somador0a5_1_s1), .s0(somador0a5_1_s0), .c(Saida_C));
endmodule

module _4to1bit (
  input  [3:0] in_1,
  output out_2
);

  and and_1 (out_2, ~in_1[0], ~in_1[1], ~in_1[2], ~in_1[3]);  // AND_Gate
endmodule

module validador_cronometro (
  input  DM,
  input  UM,
  input  DS,
  input  US,
  output DM_2,
  output UM_2,
  output DS_2,
  output US_2
);

  not not_1 (DM_2, DM);
  or or_1 (UM_2, ~DM, ~UM);  // OR_Gate
  or or_2 (DS_2, ~DM, ~UM, ~DS);  // OR_Gate
  or or_3 (US_2, ~DM, ~UM, ~DS, ~US);  // OR_Gate
endmodule

module Conversor_Negativo (
  input  [3:0] in_1,
  output neg,
  output s3,
  output s2,
  output s1,
  output s0
);

  wire and_2_out, and_3_out, and_4_out, and_5_out, and_6_out, and_7_out, and_8_out, not_1_out, not_2_out,
       not_3_out, not_4_out, not_5_out, not_6_out, not_7_out, not_8_out, not_9_out, not_10_out, not_11_out;

  not not_1 (not_1_out, in_1[2]);
  not not_2 (not_2_out, in_1[1]);
  not not_3 (not_3_out, in_1[0]);
  not not_4 (not_4_out, in_1[3]);
  not not_5 (not_5_out, in_1[1]);
  not not_6 (not_6_out, in_1[0]);
  not not_7 (not_7_out, in_1[2]);
  not not_8 (not_8_out, in_1[2]);
  not not_9 (not_9_out, in_1[3]);
  not not_10 (not_10_out, in_1[0]);
  not not_11 (not_11_out, in_1[1]);
  and and_1 (s3, in_1[3], not_1_out, not_2_out, not_3_out);
  and and_2 (and_2_out, not_4_out, in_1[2]);
  and and_3 (and_3_out, in_1[2], not_5_out, not_6_out);
  and and_4 (and_4_out, in_1[3], not_7_out, in_1[0]);
  and and_5 (and_5_out, in_1[3], not_8_out, in_1[1]);
  and and_6 (and_6_out, not_9_out, in_1[1]);
  or or_1 (s1, and_6_out, and_7_out, and_8_out);
  and and_7 (and_7_out, in_1[1], not_10_out);
  and and_8 (and_8_out, in_1[3], not_11_out, in_1[0]);
  or or_2 (s2, and_2_out, and_3_out, and_4_out, and_5_out);

  assign neg = in_1[3];
  assign s0 = in_1[0];
endmodule

module Comparador_Igualdade (
  input  [3:0] X,
  input  [3:0] XS,
  input  [3:0] Y,
  input  [3:0] YS,
  output ACERTOU
);

  wire and_1_out, and_2_out, xnor_1_out, xnor_2_out, xnor_3_out, xnor_4_out, xnor_5_out, xnor_6_out,
       xnor_7_out, xnor_8_out;

  xnor xnor_1 (xnor_1_out, XS[0], X[0]);
  xnor xnor_2 (xnor_2_out, XS[1], X[1]);
  xnor xnor_3 (xnor_3_out, YS[1], Y[1]);
  xnor xnor_4 (xnor_4_out, YS[0], Y[0]);
  xnor xnor_5 (xnor_5_out, XS[3], X[3]);
  xnor xnor_6 (xnor_6_out, XS[2], X[2]);
  xnor xnor_7 (xnor_7_out, YS[3], Y[3]);
  xnor xnor_8 (xnor_8_out, YS[2], Y[2]);
  and and_1 (and_1_out, xnor_5_out, xnor_6_out, xnor_2_out, xnor_1_out);
  and and_2 (and_2_out, xnor_7_out, xnor_8_out, xnor_3_out, xnor_4_out);
  and and_3 (ACERTOU, and_1_out, and_2_out);
endmodule

module Comparador_Desigualdade (
  input  [3:0] X,
  input  JOGAR,
  input  [3:0] Y,
  input  [3:0] XS,
  input  [3:0] YS,
  output [4:0] out_6,
  output MAIOR,
  output ACERTOU,
  output IGUAL,
  output MENOR,
  output [4:0] out_11
);

  wire and_2_out, and_3_out, and_4_out, and_5_out, and_6_out, and_7_out, and_8_out, and_9_out, and_10_out,
       and_11_out, and_12_out, and_13_out, and_14_out, and_15_out, and_16_out, and_17_out, and_18_out,
       comparador_igualdade_1_acertou, or_1_out, or_2_out, or_3_out, or_4_out, xnor_1_out, xnor_2_out,
       xnor_3_out, xnor_4_out;

  Comparador_Igualdade comparador_igualdade_1 (
    .X(X), .XS(XS), .Y(Y), .ACERTOU(comparador_igualdade_1_acertou), .YS(YS));
  Teste_de_Conversor teste_de_conversor_1 (.X(X), .Y(Y), .SAIDA(out_6));
  and and_1 (ACERTOU, JOGAR, comparador_igualdade_1_acertou);
  Teste_de_Conversor teste_de_conversor_2 (.X(XS), .Y(YS), .SAIDA(out_11));
  and and_2 (and_2_out, out_6[0], ~out_11[0]);  // AND_Gate
  and and_3 (and_3_out, out_6[1], ~out_11[1]);  // AND_Gate
  and and_4 (and_4_out, out_6[2], ~out_11[2]);  // AND_Gate
  and and_5 (and_5_out, out_6[3], ~out_11[3]);  // AND_Gate
  and and_6 (and_6_out, xnor_1_out, xnor_2_out, xnor_3_out, xnor_4_out);
  xnor xnor_1 (xnor_1_out, out_6[0], out_11[0]);
  xnor xnor_2 (xnor_2_out, out_6[1], out_11[1]);
  xnor xnor_3 (xnor_3_out, out_6[2], out_11[2]);
  xnor xnor_4 (xnor_4_out, out_6[3], out_11[3]);
  and and_7 (and_7_out, and_2_out, xnor_2_out, xnor_3_out, xnor_4_out);
  and and_8 (and_8_out, and_3_out, xnor_3_out, xnor_4_out);
  and and_9 (and_9_out, and_4_out, xnor_4_out);
  and and_10 (and_10_out, ~out_6[4], out_11[4]);  // AND_Gate
  and and_11 (and_11_out, out_6[4], ~out_11[4]);  // AND_Gate
  and and_12 (and_12_out, ~out_6[4], ~out_11[4]);  // AND_Gate
  and and_13 (and_13_out, out_6[4], out_11[4]);
  or or_1 (or_1_out, and_12_out, and_13_out);
  or or_2 (or_2_out, and_7_out, and_8_out, and_9_out, and_5_out);
  and and_14 (and_14_out, ~and_10_out, ~and_11_out, and_6_out);  // AND_Gate
  and and_15 (and_15_out, or_2_out, and_12_out);
  and and_16 (and_16_out, ~or_2_out, and_13_out);  // AND_Gate
  and and_17 (and_17_out, or_2_out, and_13_out);
  and and_18 (and_18_out, ~or_2_out, and_12_out);  // AND_Gate
  or or_3 (or_3_out, and_15_out, and_16_out, and_10_out);
  or or_4 (or_4_out, and_17_out, and_18_out, and_11_out);
  and and_19 (MAIOR, ~and_14_out, JOGAR, or_3_out);  // AND_Gate
  and and_20 (IGUAL, ~and_10_out, and_14_out, JOGAR, ~and_11_out);  // AND_Gate
  and and_21 (MENOR, ~and_14_out, JOGAR, or_4_out);  // AND_Gate
endmodule

module teste (
  input  [3:0] X,
  input  [3:0] Y,
  input  [3:0] XS,
  input  [3:0] YS,
  input  in_5,
  input  in_6,
  input  in_7,
  output [3:0] out_8,
  output MAIOR,
  output ACERTOU,
  output IGUAL,
  output MENOR,
  output [3:0] out_13
);

  wire and_1_out, and_2_out, and_3_out, and_4_out, and_6_out, and_7_out, and_8_out, and_9_out, and_10_out,
       and_11_out, and_12_out, and_13_out, and_14_out, and_15_out, and_16_out, conversor_negativo_1_neg,
       conversor_negativo_1_s0, conversor_negativo_1_s1, conversor_negativo_1_s2, conversor_negativo_1_s3,
       conversor_negativo_2_neg, conversor_negativo_2_s0, conversor_negativo_2_s1, conversor_negativo_2_s2,
       conversor_negativo_2_s3, or_1_out, or_2_out, or_3_out, xnor_1_out, xnor_2_out, xnor_3_out, xnor_4_out,
       xnor_5_out;
  wire [3:1] undriven, undriven_2;

  // Comparador_Igualdade comparador_igualdade_1: pin names not known; wires that end beside it: X, XS, Y, YS, ACERTOU
  Adder #(.width(4)) adder_1 (.a(X), .b(Y), .out(out_8));  // open: cin, cout
  Adder #(.width(4)) adder_2 (.a(XS), .b(YS), .out(out_13));  // open: cin, cout
  Conversor_Negativo conversor_negativo_1 (
    .neg(conversor_negativo_1_neg), .s3(conversor_negativo_1_s3), .s2(conversor_negativo_1_s2),
    .s1(conversor_negativo_1_s1), .s0(conversor_negativo_1_s0), .in_1({undriven, out_8[1]}));
  Conversor_Negativo conversor_negativo_2 (
    .neg(conversor_negativo_2_neg), .s3(conversor_negativo_2_s3), .s2(conversor_negativo_2_s2),
    .s1(conversor_negativo_2_s1), .s0(conversor_negativo_2_s0), .in_1({undriven_2, out_13[1]}));
  D_Flip_Flop #(.Pre_Clr_Positions("LEGACY"), .enable("true"), .NewFFLayout("false")) d_ff_1 (
    .clk(in_5), .D(in_5));  // open: Q, Qn, preset, en, reset
  and and_1 (and_1_out, conversor_negativo_1_s3, ~conversor_negativo_2_s3);  // AND_Gate
  and and_2 (and_2_out, conversor_negativo_1_s2, ~conversor_negativo_2_s2);  // AND_Gate
  and and_3 (and_3_out, conversor_negativo_1_s1, ~conversor_negativo_2_s1);  // AND_Gate
  and and_4 (and_4_out, conversor_negativo_1_s0, ~conversor_negativo_2_s0);  // AND_Gate
  and and_5 (IGUAL, xnor_1_out, xnor_2_out, xnor_3_out, xnor_4_out);
  xnor xnor_1 (xnor_1_out, conversor_negativo_1_s3, conversor_negativo_2_s3);
  xnor xnor_2 (xnor_2_out, conversor_negativo_1_s2, conversor_negativo_2_s2);
  xnor xnor_3 (xnor_3_out, conversor_negativo_1_s1, conversor_negativo_2_s1);
  xnor xnor_4 (xnor_4_out, conversor_negativo_1_s0, conversor_negativo_2_s0);
  xnor xnor_5 (xnor_5_out, in_6, in_7);
  and and_6 (and_6_out, and_1_out, xnor_2_out, xnor_3_out, xnor_4_out);
  and and_7 (and_7_out, and_2_out, xnor_3_out, xnor_4_out);
  and and_8 (and_8_out, and_3_out, xnor_4_out);
  and and_9 (and_9_out, ~conversor_negativo_1_neg, conversor_negativo_2_neg);  // AND_Gate
  and and_10 (and_10_out, conversor_negativo_1_neg, ~conversor_negativo_2_neg);  // AND_Gate
  and and_11 (and_11_out, ~conversor_negativo_1_neg, ~conversor_negativo_2_neg);  // AND_Gate
  and and_12 (and_12_out, conversor_negativo_1_neg, conversor_negativo_2_neg);
  or or_1 (or_1_out, and_6_out, and_7_out, and_8_out, and_4_out);
  and and_13 (and_13_out, or_1_out, and_11_out);
  and and_14 (and_14_out, ~or_1_out, and_12_out);  // AND_Gate
  and and_15 (and_15_out, or_1_out, and_12_out);
  and and_16 (and_16_out, ~or_1_out, and_11_out);  // AND_Gate
  or or_2 (or_2_out, and_13_out, and_14_out, and_9_out);
  or or_3 (or_3_out, and_15_out, and_16_out, and_10_out);
  and and_17 (MAIOR, ~IGUAL, or_2_out);  // AND_Gate
  and and_18 (MENOR, ~IGUAL, or_3_out);  // AND_Gate
  // Pins of 1 and 4 bits meet at {undriven_2, out_13[1]}
  // Pins of 1 and 4 bits meet at {undriven, out_8[1]}
endmodule

module PLACAR (
);

  Comparador_Desigualdade comparador_desigualdade_1 ();  // open: X, Y, XS, YS, MAIOR, ACERTOU, IGUAL, MENOR, out_6, JOGAR, out_11
endmodule

module Circuito_Core (
  input  PROXIMO,
  input  START,
  input  RESET,
  input  CHUTAR,
  input  END_A,
  input  END_B,
  input  [3:0] JA,
  input  [3:0] JB,
  output X,
  output Y,
  output COMP,
  output A,
  output B,
  output NX,
  output [3:0] X_2,
  output ACERTOU,
  output MAIOR,
  output IGUAL,
  output NY,
  output MENOR,
  output [3:0] Y_2
);

  wire adder_1_out, and_1_out, and_2_out, and_3_out, and_4_out, and_5_out, and_6_out, and_14_out,
       comparador_desigualdade_1_igual, comparador_desigualdade_1_maior, comparador_desigualdade_1_menor,
       d_ff_1_q, d_ff_1_qn, d_ff_2_q, d_ff_2_qn, demultiplexer_2_out0, demultiplexer_2_out1, nand_1_out,
       not_1_out, not_2_out, not_3_out, or_1_out, or_2_out, or_3_out, or_5_out, t_ff_1_q;
  wire [3:0] and_12_out, and_13_out, demultiplexer_1_out0, demultiplexer_1_out1, memoria_4bits_1_x,
       memoria_4bits_1_y, multiplexer_1_out, random_1_out, random_2_out;
  wire [3:3] or_4_out;

  nand nand_1 (nand_1_out, END_A, END_B);
  and and_1 (and_1_out, START, nand_1_out);
  and and_2 (and_2_out, and_1_out, PROXIMO);
  not not_1 (not_1_out, and_4_out);
  not not_2 (not_2_out, not_1_out);
  not not_3 (not_3_out, not_2_out);
  and and_3 (and_3_out, and_2_out, not_3_out, and_4_out);
  and and_4 (and_4_out, d_ff_1_qn, d_ff_2_qn);
  D_Flip_Flop #(.Pre_Clr_Positions("LEGACY"), .enable("true"), .NewFFLayout("false")) d_ff_1 (
    .clk(and_2_out), .D(adder_1_out), .Q(d_ff_1_q), .Qn(d_ff_1_qn), .reset(RESET));  // open: preset, en
  Adder #(.width(1)) adder_1 (.a(d_ff_2_q), .b(1'b1), .out(adder_1_out));  // open: cin, cout
  D_Flip_Flop #(.Pre_Clr_Positions("LEGACY"), .enable("true"), .NewFFLayout("false")) d_ff_2 (
    .clk(and_2_out), .D(d_ff_1_q), .Q(d_ff_2_q), .Qn(d_ff_2_qn), .reset(RESET));  // open: preset, en
  and and_5 (and_5_out, B, ACERTOU);
  or or_1 (or_1_out, and_5_out, END_A);
  and and_6 (and_6_out, ACERTOU, A);
  or or_2 (or_2_out, and_6_out, END_B);
  and and_7 (X, ~d_ff_2_q, d_ff_1_q);  // AND_Gate
  and and_8 (Y, d_ff_2_q, d_ff_1_q);
  and and_9 (COMP, d_ff_2_q, ~d_ff_1_q);  // AND_Gate
  T_Flip_Flop #(.Pre_Clr_Positions("LEGACY"), .enable("true"), .NewFFLayout("false")) t_ff_1 (
    .clk(and_3_out), .T(and_3_out), .Q(t_ff_1_q), .preset(or_1_out), .reset(or_3_out));  // open: Qn, en
  or or_3 (or_3_out, RESET, or_2_out);
  and and_10 (A, and_1_out, ~t_ff_1_q);  // AND_Gate
  and and_11 (B, and_1_out, t_ff_1_q);
  or or_4 (or_4_out[3], X, Y);
  assign and_12_out = JA & {4{or_4_out[3]}};  // AND_Gate and_12, 4 bits wide
  assign and_13_out = JB & {4{or_4_out[3]}};  // AND_Gate and_13, 4 bits wide
  Multiplexer #(.width(4), .enable("false")) multiplexer_1 (
    .in0(and_12_out), .in1(and_13_out), .out(multiplexer_1_out), .sel(B));
  Demultiplexer #(.width(4), .enable("false")) demultiplexer_1 (
    .out0(demultiplexer_1_out0), .out1(demultiplexer_1_out1), .in(multiplexer_1_out), .sel(Y));
  Demultiplexer #(.enable("false")) demultiplexer_2 (
    .out0(demultiplexer_2_out0), .out1(demultiplexer_2_out1), .in(CHUTAR), .sel(Y));
  Memoria_4bits memoria_4bits_1 (
    .EX(demultiplexer_1_out0), .CLK_X(demultiplexer_2_out0), .RESET(RESET), .EY(demultiplexer_1_out1),
    .CLK_Y(demultiplexer_2_out1), .X(memoria_4bits_1_x), .Y(memoria_4bits_1_y));
  Conversor_Negativo conversor_negativo_1 (
    .neg(NX), .s3(X_2[3]), .s2(X_2[2]), .s1(X_2[1]), .s0(X_2[0]), .in_1(memoria_4bits_1_x));
  Conversor_Negativo conversor_negativo_2 (
    .neg(NY), .s3(Y_2[3]), .s2(Y_2[2]), .s1(Y_2[1]), .s0(Y_2[0]), .in_1(memoria_4bits_1_y));
  Random #(.width(4), .seed(1)) random_1 (.clk(or_5_out), .out(random_1_out));  // open: next, clr
  Random #(.width(4)) random_2 (.clk(or_5_out), .out(random_2_out));  // open: next, clr
  or or_5 (or_5_out, RESET, and_14_out);
  Comparador_Desigualdade comparador_desigualdade_1 (
    .X(memoria_4bits_1_x), .Y(memoria_4bits_1_y), .XS(random_1_out), .YS(random_2_out),
    .MAIOR(comparador_desigualdade_1_maior), .ACERTOU(ACERTOU), .IGUAL(comparador_desigualdade_1_igual),
    .MENOR(comparador_desigualdade_1_menor), .JOGAR(COMP));  // open: out_6, out_11
  and and_14 (and_14_out, ACERTOU, ~COMP);  // AND_Gate
  and and_15 (MAIOR, comparador_desigualdade_1_maior, START);
  and and_16 (IGUAL, comparador_desigualdade_1_igual, START);
  and and_17 (MENOR, comparador_desigualdade_1_menor, START);

  // Other names for the same wires on the sheet: A___JOGANDO = A; B___JOGANDO = B; CHUTANDO_X = X; CHUTANDO_Y = Y;
  //   EMJOGO = START; ENDA = END_A; ENDB = END_B
endmodule

module Memoria_4bits (
  input  [3:0] EX,
  input  CLK_X,
  input  RESET,
  input  [3:0] EY,
  input  CLK_Y,
  output [3:0] X,
  output [3:0] Y
);

  wire not_1_out, not_2_out, not_3_out, not_4_out, not_5_out, not_6_out, not_7_out, not_8_out;

  not not_1 (not_1_out, CLK_X);
  not not_2 (not_2_out, not_1_out);
  not not_3 (not_3_out, CLK_Y);
  not not_4 (not_4_out, not_3_out);
  not not_5 (not_5_out, not_2_out);
  not not_6 (not_6_out, not_5_out);
  not not_7 (not_7_out, not_4_out);
  not not_8 (not_8_out, not_7_out);
  D_Flip_Flop #(.Pre_Clr_Positions("LEGACY"), .enable("true"), .NewFFLayout("false")) d_ff_1 (
    .clk(not_6_out), .D(EX[3]), .Q(X[3]), .reset(RESET));  // open: Qn, preset, en
  D_Flip_Flop #(.Pre_Clr_Positions("LEGACY"), .enable("true"), .NewFFLayout("false")) d_ff_2 (
    .clk(not_8_out), .D(EY[3]), .Q(Y[3]), .reset(RESET));  // open: Qn, preset, en
  D_Flip_Flop #(.Pre_Clr_Positions("LEGACY"), .enable("true"), .NewFFLayout("false")) d_ff_3 (
    .clk(not_6_out), .D(EX[2]), .Q(X[2]), .reset(RESET));  // open: Qn, preset, en
  D_Flip_Flop #(.Pre_Clr_Positions("LEGACY"), .enable("true"), .NewFFLayout("false")) d_ff_4 (
    .clk(not_8_out), .D(EY[2]), .Q(Y[2]), .reset(RESET));  // open: Qn, preset, en
  D_Flip_Flop #(.Pre_Clr_Positions("LEGACY"), .enable("true"), .NewFFLayout("false")) d_ff_5 (
    .clk(not_6_out), .D(EX[1]), .Q(X[1]), .reset(RESET));  // open: Qn, preset, en
  D_Flip_Flop #(.Pre_Clr_Positions("LEGACY"), .enable("true"), .NewFFLayout("false")) d_ff_6 (
    .clk(not_8_out), .D(EY[1]), .Q(Y[1]), .reset(RESET));  // open: Qn, preset, en
  D_Flip_Flop #(.Pre_Clr_Positions("LEGACY"), .enable("true"), .NewFFLayout("false")) d_ff_7 (
    .clk(not_6_out), .D(EX[0]), .Q(X[0]), .reset(RESET));  // open: Qn, preset, en
  D_Flip_Flop #(.Pre_Clr_Positions("LEGACY"), .enable("true"), .NewFFLayout("false")) d_ff_8 (
    .clk(not_8_out), .D(EY[0]), .Q(Y[0]), .reset(RESET));  // open: Qn, preset, en
endmodule

module Placar (
  input  ACERTOU,
  input  A___JOGANDO,
  input  B___JOGANDO,
  input  RESET,
  input  END_A,
  input  END_B,
  output FIM_DE_JOGO,
  output A_Ganhou,
  output EMPATE,
  output B_Ganhou,
  output [3:0] Placar_A,
  output [3:0] Placar_B
);

  wire A_Acertou, A_VENCEU, and_3_out, and_4_out, and_5_out, and_6_out, and_7_out, and_8_out, and_9_out,
       and_10_out, and_11_out, and_14_out, and_16_out, B_Acertou, B_VENCEU, or_1_out, xnor_1_out, xnor_2_out,
       xnor_3_out, xnor_4_out;
  wire [3:0] adder_1_out, adder_2_out;

  and and_1 (A_Acertou, ACERTOU, A___JOGANDO);
  and and_2 (B_Acertou, ACERTOU, B___JOGANDO);
  xnor xnor_1 (xnor_1_out, Placar_A[0], Placar_B[0]);
  and and_3 (and_3_out, Placar_A[0], ~Placar_B[0]);  // AND_Gate
  xnor xnor_2 (xnor_2_out, Placar_A[1], Placar_B[1]);
  and and_4 (and_4_out, Placar_A[1], ~Placar_B[1]);  // AND_Gate
  xnor xnor_3 (xnor_3_out, Placar_A[2], Placar_B[2]);
  and and_5 (and_5_out, Placar_A[2], ~Placar_B[2]);  // AND_Gate
  xnor xnor_4 (xnor_4_out, Placar_A[3], Placar_B[3]);
  and and_6 (and_6_out, Placar_A[3], ~Placar_B[3]);  // AND_Gate
  D_Flip_Flop #(.Pre_Clr_Positions("LEGACY"), .enable("true"), .NewFFLayout("false")) d_ff_1 (
    .clk(A_Acertou), .D(adder_1_out[3]), .Q(Placar_A[3]), .reset(RESET));  // open: Qn, preset, en
  D_Flip_Flop #(.Pre_Clr_Positions("LEGACY"), .enable("true"), .NewFFLayout("false")) d_ff_2 (
    .clk(B_Acertou), .D(adder_2_out[3]), .Q(Placar_B[3]), .reset(RESET));  // open: Qn, preset, en
  and and_7 (and_7_out, xnor_1_out, xnor_2_out, xnor_3_out, xnor_4_out);
  D_Flip_Flop #(.Pre_Clr_Positions("LEGACY"), .enable("true"), .NewFFLayout("false")) d_ff_3 (
    .clk(A_Acertou), .D(adder_1_out[2]), .Q(Placar_A[2]), .reset(RESET));  // open: Qn, preset, en
  D_Flip_Flop #(.Pre_Clr_Positions("LEGACY"), .enable("true"), .NewFFLayout("false")) d_ff_4 (
    .clk(B_Acertou), .D(adder_2_out[2]), .Q(Placar_B[2]), .reset(RESET));  // open: Qn, preset, en
  and and_8 (and_8_out, and_3_out, xnor_2_out, xnor_3_out, xnor_4_out);
  and and_9 (and_9_out, and_4_out, xnor_3_out, xnor_4_out);
  and and_10 (and_10_out, and_5_out, xnor_4_out);
  D_Flip_Flop #(.Pre_Clr_Positions("LEGACY"), .enable("true"), .NewFFLayout("false")) d_ff_5 (
    .clk(A_Acertou), .D(adder_1_out[1]), .Q(Placar_A[1]), .reset(RESET));  // open: Qn, preset, en
  D_Flip_Flop #(.Pre_Clr_Positions("LEGACY"), .enable("true"), .NewFFLayout("false")) d_ff_6 (
    .clk(B_Acertou), .D(adder_2_out[1]), .Q(Placar_B[1]), .reset(RESET));  // open: Qn, preset, en
  and and_11 (and_11_out, END_A, END_B);
  or or_1 (or_1_out, and_8_out, and_9_out, and_10_out, and_6_out);
  D_Flip_Flop #(.Pre_Clr_Positions("LEGACY"), .enable("true"), .NewFFLayout("false")) d_ff_7 (
    .clk(A_Acertou), .D(adder_1_out[0]), .Q(Placar_A[0]), .reset(RESET));  // open: Qn, preset, en
  D_Flip_Flop #(.Pre_Clr_Positions("LEGACY"), .enable("true"), .NewFFLayout("false")) d_ff_8 (
    .clk(B_Acertou), .D(adder_2_out[0]), .Q(Placar_B[0]), .reset(RESET));  // open: Qn, preset, en
  and and_12 (A_VENCEU, Placar_A[3], Placar_A[2], Placar_A[1], Placar_A[0]);
  and and_13 (B_VENCEU, Placar_B[3], Placar_B[2], Placar_B[1], Placar_B[0]);
  and and_14 (and_14_out, ~and_7_out, and_11_out, or_1_out);  // AND_Gate
  and and_15 (EMPATE, and_7_out, and_11_out);
  and and_16 (and_16_out, ~and_7_out, and_11_out, ~or_1_out);  // AND_Gate
  Adder #(.width(4)) adder_1 (.a(4'b0001), .b(Placar_A), .out(adder_1_out));  // open: cin, cout
  Adder #(.width(4)) adder_2 (.a(4'b0001), .b(Placar_B), .out(adder_2_out));  // open: cin, cout
  or or_2 (A_Ganhou, and_14_out, A_VENCEU);
  or or_3 (B_Ganhou, and_16_out, B_VENCEU);
  or or_4 (FIM_DE_JOGO, and_11_out, B_VENCEU, A_VENCEU);
endmodule

module Conversor_4Bits_N (
  input  [3:0] ENTRADA,
  output N,
  output [3:0] num
);

  wire [3:0] xor_4_out;

  xor xor_1 (xor_4_out[3], ENTRADA[3], ENTRADA[3]);
  xor xor_2 (xor_4_out[2], ENTRADA[3], ENTRADA[2]);
  xor xor_3 (xor_4_out[1], ENTRADA[3], ENTRADA[1]);
  xor xor_4 (xor_4_out[0], ENTRADA[3], ENTRADA[0]);
  Adder #(.width(4)) adder_1 (.a({3'b000, ENTRADA[3]}), .b(xor_4_out), .out(num));  // open: cin, cout

  assign N = ENTRADA[3];
endmodule

module Multiplexador_4bits (
  input  [3:0] A,
  input  [3:0] B,
  input  Seletor,
  output [3:0] SAIDA
);

  wire [3:0] and_1_out, and_2_out;

  assign and_1_out = A & ~{4{Seletor}};  // AND_Gate and_1, 4 bits wide
  assign and_2_out = B & {4{Seletor}};  // AND_Gate and_2, 4 bits wide
  assign SAIDA = and_1_out | and_2_out;  // OR_Gate or_1, 4 bits wide
endmodule

module Teste_de_Conversor (
  input  [3:0] X,
  input  [3:0] Y,
  output [4:0] SAIDA
);

  wire and_1_out, and_2_out, and_3_out, and_4_out, conversor_4bits_n_1_n, conversor_4bits_n_2_n,
       conversor_4bits_n_3_n, conversor_4bits_n_4_n, conversor_4bits_n_5_n, xor_1_out;
  wire [3:0] adder_1_out, adder_2_out, conversor_4bits_n_1_num, conversor_4bits_n_2_num,
       conversor_4bits_n_3_num, conversor_4bits_n_4_num, conversor_4bits_n_5_num, seletor_4bits_1_saida_a,
       seletor_4bits_1_saida_b, seletor_4bits_2_saida_a, seletor_4bits_2_saida_b, seletor_4bits_3_saida_a,
       seletor_4bits_3_saida_b, seletor_4bits_4_saida_a, seletor_4bits_4_saida_b, subtractor_1_out,
       subtractor_2_out;

  Conversor_4Bits_N conversor_4bits_n_1 (.ENTRADA(X), .N(conversor_4bits_n_1_n), .num(conversor_4bits_n_1_num));
  Conversor_4Bits_N conversor_4bits_n_2 (.ENTRADA(Y), .N(conversor_4bits_n_2_n), .num(conversor_4bits_n_2_num));
  xor xor_1 (xor_1_out, conversor_4bits_n_2_n, conversor_4bits_n_1_n);
  and and_1 (and_1_out, conversor_4bits_n_1_n, conversor_4bits_n_2_n);
  and and_2 (and_2_out, conversor_4bits_n_1_n, xor_1_out);
  and and_3 (and_3_out, conversor_4bits_n_2_n, xor_1_out);
  and and_4 (and_4_out, ~conversor_4bits_n_1_n, ~conversor_4bits_n_2_n);  // AND_Gate
  Seletor_4Bits seletor_4bits_1 (
    .A(conversor_4bits_n_2_num), .B(conversor_4bits_n_1_num), .Seletor(and_1_out),
    .SAIDA_A(seletor_4bits_1_saida_a), .SAIDA_B(seletor_4bits_1_saida_b));
  Seletor_4Bits seletor_4bits_2 (
    .A(conversor_4bits_n_2_num), .B(conversor_4bits_n_1_num), .Seletor(and_2_out),
    .SAIDA_A(seletor_4bits_2_saida_a), .SAIDA_B(seletor_4bits_2_saida_b));
  Seletor_4Bits seletor_4bits_3 (
    .A(conversor_4bits_n_1_num), .B(conversor_4bits_n_2_num), .Seletor(and_3_out),
    .SAIDA_A(seletor_4bits_3_saida_a), .SAIDA_B(seletor_4bits_3_saida_b));
  Seletor_4Bits seletor_4bits_4 (
    .A(conversor_4bits_n_2_num), .B(conversor_4bits_n_1_num), .Seletor(and_4_out),
    .SAIDA_A(seletor_4bits_4_saida_a), .SAIDA_B(seletor_4bits_4_saida_b));
  Conversor_4Bits_N conversor_4bits_n_3 (
    .ENTRADA(adder_1_out), .N(conversor_4bits_n_3_n), .num(conversor_4bits_n_3_num));
  Adder #(.width(4)) adder_1 (
    .a(seletor_4bits_1_saida_a), .b(seletor_4bits_1_saida_b), .out(adder_1_out));  // open: cin, cout
  Conversor_4Bits_N conversor_4bits_n_4 (
    .ENTRADA(subtractor_1_out), .N(conversor_4bits_n_4_n), .num(conversor_4bits_n_4_num));
  Subtractor #(.width(4)) subtractor_1 (
    .a(seletor_4bits_2_saida_a), .b(seletor_4bits_2_saida_b), .out(subtractor_1_out));  // open: bin, bout
  Conversor_4Bits_N conversor_4bits_n_5 (
    .ENTRADA(subtractor_2_out), .N(conversor_4bits_n_5_n), .num(conversor_4bits_n_5_num));
  Subtractor #(.width(4)) subtractor_2 (
    .a(seletor_4bits_3_saida_a), .b(seletor_4bits_3_saida_b), .out(subtractor_2_out));  // open: bin, bout
  Adder #(.width(4)) adder_2 (
    .a(seletor_4bits_4_saida_a), .b(seletor_4bits_4_saida_b), .out(adder_2_out));  // open: cin, cout
  or or_1 (SAIDA[4], conversor_4bits_n_3_n, conversor_4bits_n_4_n, conversor_4bits_n_5_n);
  assign SAIDA[3:0] = adder_2_out | conversor_4bits_n_3_num | conversor_4bits_n_4_num | conversor_4bits_n_5_num;  // OR_Gate or_2, 4 bits wide
endmodule

module Seletor_4Bits (
  input  [3:0] A,
  input  [3:0] B,
  input  Seletor,
  output [3:0] SAIDA_A,
  output [3:0] SAIDA_B
);

  assign SAIDA_A = A & {4{Seletor}};  // AND_Gate and_1, 4 bits wide
  assign SAIDA_B = B & {4{Seletor}};  // AND_Gate and_2, 4 bits wide
endmodule
